# Fritzing sketch ArduinoR4MinimaCanBusRelayBoard (saved by Fritzing 0.9.3b)

parts:
  U1 = 4-Channel 5v Relay Shield [package=relay-4ch5v10a]
  J1 = Camdenboss CTB0158-3 [part_number=CTB0158-3 package=THT]
  J5 = Camdenboss CTB0158-3 [part_number=CTB0158-3 package=THT]
  J6 = Camdenboss CTB0158-3 [part_number=CTB0158-3 package=THT]
  J7 = Camdenboss CTB0158-3 [part_number=CTB0158-3 package=THT]
  J8 = Camdenboss CTB0158-3 [part_number=CTB0158-3 package=THT]
  J9 = Camdenboss CTB0158-4 [part_number=CTB0158-4 package=THT]
  JP1 = Jumper [package=sj_2s]
  J10 = Camdenboss CTB0158-5 [part_number=CTB0158-5 package=THT]
  M3 = SN65HVD230 CAN Bus transciever module [package=THT]
  A1 = Arduino R4 Minima
  J11 = Camdenboss CTB0158-3 [part_number=CTB0158-3 package=THT]
  J3 = screw terminal, 2 pins
  R1 = Resistor [tolerance=±5% resistance=120 package="0805 [SMD]"]

nets:
  N1: U1.VCC, J1.terminal_2, J5.terminal_2, J6.terminal_2, J7.terminal_2, J8.terminal_2, A1.Pin_5, J11.terminal_2
  N2: U1.GND, J1.terminal_1, J5.terminal_1, J6.terminal_1, J7.terminal_1, J8.terminal_1, J9.terminal_2, M3.pin_2, A1.Pin_6, A1.Pin_45, J11.terminal_1
  N3: U1.IN1, A1.Pin_40
  N4: U1.IN2, A1.Pin_39
  N5: U1.K1-In, U1.K2-In, U1.K3-In, U1.K4-In, J3.pin1
  N6: U1.K1-On, J10.pin4
  N7: U1.K2-On, J10.pin3
  N8: U1.IN4, A1.Pin_37
  N9: U1.K3-On, J10.pin2
  N10: U1.K4-On, J10.pin1
  N11: U1.IN3, A1.Pin_38
  N12: J1.terminal_3, A1.Pin_13
  N13: J5.terminal_3, A1.Pin_9
  N14: J6.terminal_3, A1.Pin_10
  N15: J7.terminal_3, A1.Pin_11
  N16: J8.terminal_3, A1.Pin_12
  N17: J9.terminal_1, A1.Pin_8
  N18: J9.terminal_3, M3.pin_5, R1.Pin_0
  N19: J9.terminal_4, JP1.1, M3.pin_6
  N20: JP1.2, R1.Pin_1
  N21: J10.pin5, J3.pin2
  N22: M3.pin_1, A1.Pin_4
  N23: M3.pin_3, A1.Pin_35
  N24: M3.pin_4, A1.Pin_36
  N25: A1.Pin_14, J11.terminal_3

notes:
  12V power & canbus
  120 ohm terminator resistor jumper
  12V
  Solenoids connector
  5V analog pressure sensors
  Normally Open
  SN65HVD230
  for canbus
  On All relays

custom parts:
  4-Channel 5v Relay Shield: 4 Channel 5v Relay Shield w. 2x SPD-06VDC-SD-C
  SN65HVD230 CAN Bus transciever module: Bus Transceiver SN65HVD230 CAN Communication Module, for Arduino.
  Arduino R4 Minima: Introducing the Arduino UNO R4 Minima! This board boasts the RA4M1 microprocessor from Renesas, delivering increased processing power, expanded memory, and additional peripherals.
